# Fritzing sketch circuit (saved by Fritzing 0.9.3b)
breadboards: 1

parts:
  Εξάρτημα1 = Arduino Uno (Rev3)
  DHT11_1 = DHT11 module
  S1 = Pushbutton [package="[THT]"]
  S2 = Pushbutton [package="[THT]"]
  R1 = Resistor [tolerance=±5% resistance=10k package=THT]
  R3 = Resistor [tolerance=±5% resistance=220 package=THT]
  LED1 = LED - 5mm [color="White (6500K)" package="5 mm [THT]"]
  LED2 = LED - 5mm [color="White (6500K)" package="5 mm [THT]"]
  R4 = Resistor [tolerance=±5% resistance=220 package=THT]
  R5 = Resistor [tolerance=±5% resistance=10k package=THT]
  LCD2004-I2C1 = LCD2004-I2C

nets:
  N1: Εξάρτημα1.A4/SDA, LCD2004-I2C1.SDA
  N2: Εξάρτημα1.A5/SCL, LCD2004-I2C1.SCL
  N3: Εξάρτημα1.D9_PWM, S1.Pin_3, S1.Pin_4, R5.Pin_1
  N4: Εξάρτημα1.D10_PWM/SS, S2.Pin_3, S2.Pin_4, R1.Pin_1
  N5: Εξάρτημα1.D2, LED1.anode
  N6: Εξάρτημα1.D3_PWM, LED2.anode
  N7: Εξάρτημα1.D5_PWM, DHT11_1.DATA
  5V: Εξάρτημα1.5V, DHT11_1.VCC, S1.Pin_1, S1.Pin_2, S2.Pin_1, S2.Pin_2
  GND: Εξάρτημα1.GND, DHT11_1.GND, R1.Pin_0, R3.Pin_0, R5.Pin_0
  N8: R3.Pin_1, LED1.cathode
  N9: LED2.cathode, R4.Pin_1

custom parts:
  DHT11 module: https://cdn-learn.adafruit.com/downloads/pdf/dht.pdf DHT11 black pcb module reference by:https://github.com/adafruit/Fritzing-Library/blob/master/parts/DHT11%20Humitidy%20and%20Temperature%20Sensor.fzpz
  LCD2004-I2C: A standard character display with 4x20 characters. Comes in many colors with LCM2004 IIC attached.
